# Fritzing sketch 0.1 (saved by Fritzing 0.9.3b)
perfboards: 1

parts:
  ORP_Circuit1 = ORP Circuit  # not connected
  D_O_Circuit1 = D.O. Circuit  # not connected
  Pre-Assembled_Female_BNC1 = Pre-Assembled Female BNC  # not connected
  Pre-Assembled_Female_BNC2 = Pre-Assembled Female BNC  # not connected
  U1 = NodeMCU V1.0  # not connected
  U2 = Header 10 [package=1x10-2mm-smd]
  DHT1 = DHT22 Humidity and Temperature Sensor
  DS1 = DS18B20 1-Wire Temperature Sensor [part_number=DS18B20]

nets:
  N1: U2.3, DS1.VDD
  N2: U2.4, DS1.DQ
  N3: U2.5, DS1.GND
  N4: U2.7, DHT1.GND
  N5: U2.8, DHT1.NULL
  N6: U2.9, DHT1.DATA
  N7: U2.10, DHT1.VDD

notes:
  - La scheda è più grande, comprende anche le due linee blu laterali.
  - Le linee nere sono le divisirie.
  Breadbord V0.2
  Acquaponica

custom parts:
  NodeMCU V1.0: ESP8266 based NodeMCU
