# Fritzing sketch breadBoard (saved by Fritzing 0.9.3b)
perfboards: 1

parts:
  ORP_Circuit1 = ORP Circuit  # not connected
  D_O_Circuit1 = D.O. Circuit  # not connected
  Pre-Assembled_Female_BNC1 = Pre-Assembled Female BNC  # not connected
  Pre-Assembled_Female_BNC2 = Pre-Assembled Female BNC  # not connected
  U1 = NodeMCU V1.0  # not connected
  U2 = Header 10 [package=1x10-2mm-smd]
  DHT1 = DHT22 Humidity and Temperature Sensor
  DS1 = DS18B20 1-Wire Temperature Sensor [part_number=DS18B20]
  Part1 = OLED Monochrome 128x64 1.3 inch [part_number=938]
  U3 = Header 6 [package=1x06_smd_straight_alt]

nets:
  N1: U2.3, DS1.VDD
  N2: U2.4, DS1.DQ
  N3: U2.5, DS1.GND
  N4: U2.7, DHT1.GND
  N5: U2.8, DHT1.NULL
  N6: U2.9, DHT1.DATA
  N7: U2.10, DHT1.VDD
  N8: Part1.MOSI_SDA, U3.4
  N9: Part1.SCLK_SCK, U3.3
  N10: Part1.3.3V, U3.1
  N11: Part1.GND, U3.5

notes:
  - La scheda è più grande, comprende anche le due linee blu laterali.
  - Le linee nere sono le divisirie.
  Breadbord V0.3
  Acquaponica

custom parts:
  NodeMCU V1.0: ESP8266 based NodeMCU
  OLED Monochrome 128x64 1.3 inch: These displays are small, only about 1.3" diagonal, but very readable due to the high contrast of an OLED display. This display is made of 128x64 individual white OLED pixels, each one is turned on or off by the controller chip. Because the display makes its own light, no backlight is required. This reduces the power required to run the OLED and is why the display has such high contrast; we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
